// Logisim project tragamonedas.circ as structural Verilog: 3 circuits, main circuit main
module main (
  output out_1
);

  wire clock_1_out;
  wire [1:0] counter_1_q, joystick_1_y;
  wire [6:0] imagerom_1_out_2, imagerom_1_out_3, imagerom_1_out_4, imagerom_1_out_5, imagerom_1_out_6,
       imagerom_2_out_2, imagerom_2_out_3, imagerom_2_out_4, imagerom_2_out_5, imagerom_2_out_6,
       imagerom_3_out_2, imagerom_3_out_3, imagerom_3_out_4, imagerom_3_out_5, imagerom_3_out_6;

  Counter #(.width(2), .max('h3)) counter_1 (.Q(counter_1_q), .clk(clock_1_out));  // open: load, D, count, carry, clr
  Clock clock_1 (.out(clock_1_out));
  // Probe on joystick_1_y
  Joystick #(.bits(2)) joystick_1 (.y(joystick_1_y));  // open: x
  DotMatrix dotmatrix_1 (
    .col0(imagerom_2_out_2), .col1(imagerom_2_out_3), .col2(imagerom_2_out_4), .col3(imagerom_2_out_5),
    .col4(imagerom_2_out_6));
  DotMatrix dotmatrix_2 (
    .col0(imagerom_1_out_2), .col1(imagerom_1_out_3), .col2(imagerom_1_out_4), .col3(imagerom_1_out_5),
    .col4(imagerom_1_out_6));
  ImageROM imagerom_1 (
    .in_1(counter_1_q), .out_2(imagerom_1_out_2), .out_3(imagerom_1_out_3), .out_4(imagerom_1_out_4),
    .out_5(imagerom_1_out_5), .out_6(imagerom_1_out_6));
  ImageROM imagerom_2 (
    .in_1(counter_1_q), .out_2(imagerom_2_out_2), .out_3(imagerom_2_out_3), .out_4(imagerom_2_out_4),
    .out_5(imagerom_2_out_5), .out_6(imagerom_2_out_6));
  controlador_palanca Controlador_Palanca (.in_1(joystick_1_y), .out_2(out_1));
  DotMatrix dotmatrix_3 (
    .col0(imagerom_3_out_2), .col1(imagerom_3_out_3), .col2(imagerom_3_out_4), .col3(imagerom_3_out_5),
    .col4(imagerom_3_out_6));
  ImageROM imagerom_3 (
    .in_1(counter_1_q), .out_2(imagerom_3_out_2), .out_3(imagerom_3_out_3), .out_4(imagerom_3_out_4),
    .out_5(imagerom_3_out_5), .out_6(imagerom_3_out_6));
  LED \Detección_Palanca  (.in(out_1));
endmodule

module ImageROM (
  input  [1:0] in_1,
  output [6:0] out_2,
  output [6:0] out_3,
  output [6:0] out_4,
  output [6:0] out_5,
  output [6:0] out_6
);

  ROM #(.addrWidth(2), .dataWidth(7)) rom_1 (.addr(in_1), .data(out_2));  // open: sel
  ROM #(.addrWidth(2), .dataWidth(7)) rom_2 (.addr(in_1), .data(out_3));  // open: sel
  ROM #(.addrWidth(2), .dataWidth(7)) rom_3 (.addr(in_1), .data(out_4));  // open: sel
  ROM #(.addrWidth(2), .dataWidth(7)) rom_4 (.addr(in_1), .data(out_5));  // open: sel
  ROM #(.addrWidth(2), .dataWidth(7)) rom_5 (.addr(in_1), .data(out_6));  // open: sel

  // Notes on the sheet:
  //   contents of rom_1 (hex, n*v repeats v):
  //   40 6 8
  //   contents of rom_2 (hex, n*v repeats v):
  //   43 3e 1b
  //   contents of rom_3 (hex, n*v repeats v):
  //   4c 7f 3e
  //   contents of rom_4 (hex, n*v repeats v):
  //   58 3e 6c
  //   contents of rom_5 (hex, n*v repeats v):
  //   60 6 8
endmodule

module controlador_palanca (
  input  [1:0] in_1,
  output out_2
);

  and and_1 (out_2, in_1[0], in_1[1]);
endmodule
